# Fritzing sketch Regelsysteem wiring (saved by Fritzing 0.9.3b)
breadboards: 2

parts:
  Onderdeel1 = Arduino Due (Rev2b)
  Q1 = NPN-Transistor [package="TO92 [THT]"]
  Q2 = NPN-Transistor [package="TO92 [THT]"]
  R1 = Resistor [tolerance=±5% resistance=220 package=THT]
  R2 = Resistor [tolerance=±5% resistance=220 package=THT]
  U1 = Battery Holders [package=lipo-1100mAh]
  S1 = SWITCH-MOMENTARY-2 [package=tactile-pth]
  S2 = SWITCH-MOMENTARY-2 [package=tactile-pth]
  R3 = Resistor [tolerance=±5% resistance=220 package=THT]
  R4 = Resistor [tolerance=±5% resistance=220 package=THT]
  R5 = Resistor [tolerance=±5% resistance=220 package=THT]

nets:
  N1: Onderdeel1.5V, R2.Pin_0, R3.Pin_1, R4.Pin_1, R5.Pin_0
  N2: Onderdeel1.GND, Q1.C, Q2.C, U1.-, S1.1, S2.1
  N3: Onderdeel1.D9_PWM, R1.Pin_0
  N4: Onderdeel1.D2_PWM, R5.Pin_1
  N5: Onderdeel1.D22, S1.2
  N6: Onderdeel1.D24, S2.2
  N7: Q1.E, Q2.E, R2.Pin_1
  N8: Q1.B, Q2.B, R1.Pin_1

notes:
  Lipo moet DC-unit voorstellen van 12V
  4 wired fan:
  Red: Vcc
  Black: Ground
  Blue: Pwm signal
  Yellow: Tach wire
  Afstandssensor ToF:
  Yellow: SCL
  Blue: SDA
  Black: Ground
  Red: Vcc
